// Logisim project mco1.circ as structural Verilog: 3 circuits, main circuit main
module main (
  input  in_1,
  input  in_2,
  input  in_3,
  input  in_4
);

  wire code_128_nand_1_b1, code_128_nand_1_b2, code_128_nand_1_b3, code_128_nand_1_b4, code_128_nand_1_b5,
       code_128_nand_1_b6, code_128_nand_1_b7, code_128_nand_1_b8, code_128_nand_1_b9, code_128_nand_1_b10,
       code_128_nand_1_b11;

  code_128_NAND code_128_nand_1 (
    .i1(in_1), .i2(in_2), .i3(in_3), .i4(in_4), .b1(code_128_nand_1_b1), .b2(code_128_nand_1_b2),
    .b3(code_128_nand_1_b3), .b4(code_128_nand_1_b4), .b5(code_128_nand_1_b5), .b6(code_128_nand_1_b6),
    .b7(code_128_nand_1_b7), .b8(code_128_nand_1_b8), .b9(code_128_nand_1_b9), .b10(code_128_nand_1_b10),
    .b11(code_128_nand_1_b11));
  LED led_1 (.in(code_128_nand_1_b1));
  LED led_2 (.in(code_128_nand_1_b5));
  LED led_3 (.in(code_128_nand_1_b2));
  LED led_4 (.in(code_128_nand_1_b4));
  LED led_5 (.in(code_128_nand_1_b3));
  LED led_6 (.in(code_128_nand_1_b9));
  LED led_7 (.in(code_128_nand_1_b8));
  LED led_8 (.in(code_128_nand_1_b7));
  LED led_9 (.in(code_128_nand_1_b6));
  LED led_10 (.in(code_128_nand_1_b10));
  LED led_11 (.in(code_128_nand_1_b11));
endmodule

module code128 (
  input  i1,
  input  i2,
  input  i3,
  input  i4,
  output b1,
  output b2,
  output b3,
  output b4,
  output b5,
  output b6,
  output b7,
  output b8,
  output b9,
  output b10,
  output b11
);

  wire and_1_out, and_2_out, and_3_out, and_4_out, and_5_out, and_6_out, and_7_out, and_8_out, and_9_out,
       and_10_out, and_11_out, and_12_out, and_13_out, and_14_out, and_15_out, and_16_out, and_17_out,
       and_18_out, and_19_out, and_20_out, and_21_out, and_22_out, and_23_out, and_24_out, and_25_out,
       and_26_out, and_27_out, and_28_out, and_29_out, and_30_out, not_1_out, not_2_out, not_3_out,
       not_4_out, not_5_out, not_6_out, not_7_out, not_8_out, not_9_out, not_10_out, not_11_out, not_12_out,
       not_13_out, not_14_out, not_15_out, not_16_out, not_17_out, not_18_out, not_19_out, not_20_out,
       not_21_out, not_22_out, not_23_out, not_24_out, not_25_out, not_26_out, not_27_out, not_28_out,
       not_29_out, not_30_out, not_31_out, not_32_out, not_33_out, not_34_out, not_35_out, not_36_out,
       not_37_out, not_38_out, not_39_out, not_40_out, not_41_out, not_42_out, not_43_out, not_44_out,
       not_45_out;

  not not_1 (not_1_out, i1);
  not not_2 (not_2_out, i2);
  and and_1 (and_1_out, not_1_out, not_2_out, not_3_out);
  not not_3 (not_3_out, i3);
  not not_4 (not_4_out, i2);
  and and_2 (and_2_out, not_4_out, i3, not_5_out);
  not not_5 (not_5_out, i4);
  and and_3 (and_3_out, i1, not_6_out, i4);
  not not_6 (not_6_out, i2);
  not not_7 (not_7_out, i3);
  not not_8 (not_8_out, i4);
  not not_9 (not_9_out, i1);
  not not_10 (not_10_out, i3);
  and and_4 (and_4_out, not_9_out, not_10_out, not_11_out);
  not not_11 (not_11_out, i4);
  not not_12 (not_12_out, i1);
  and and_5 (and_5_out, not_12_out, i3, i4);
  and and_6 (and_6_out, i2, not_13_out);
  not not_13 (not_13_out, i4);
  and and_7 (and_7_out, i1, i2);
  not not_14 (not_14_out, i2);
  and and_8 (and_8_out, not_14_out, not_15_out);
  not not_15 (not_15_out, i3);
  and and_9 (and_9_out, i3, not_16_out);
  not not_16 (not_16_out, i4);
  and and_10 (and_10_out, i2, i4);
  not not_17 (not_17_out, i1);
  not not_18 (not_18_out, i2);
  not not_19 (not_19_out, i3);
  not not_20 (not_20_out, i1);
  not not_21 (not_21_out, i2);
  not not_22 (not_22_out, i4);
  not not_23 (not_23_out, i2);
  not not_24 (not_24_out, i3);
  not not_25 (not_25_out, i4);
  not not_26 (not_26_out, i2);
  not not_27 (not_27_out, i1);
  not not_28 (not_28_out, i2);
  not not_29 (not_29_out, i3);
  not not_30 (not_30_out, i1);
  and and_11 (and_11_out, not_30_out, not_31_out);
  not not_31 (not_31_out, i3);
  not not_32 (not_32_out, i1);
  and and_12 (and_12_out, not_32_out, not_33_out, i4);
  not not_33 (not_33_out, i2);
  not not_34 (not_34_out, i3);
  and and_13 (and_13_out, not_34_out, i4);
  and and_14 (and_14_out, i2, not_35_out);
  not not_35 (not_35_out, i4);
  and and_15 (and_15_out, i1, i2);
  not not_36 (not_36_out, i1);
  and and_16 (and_16_out, not_36_out, not_37_out);
  not not_37 (not_37_out, i3);
  not not_38 (not_38_out, i2);
  and and_17 (and_17_out, not_38_out, not_39_out);
  not not_39 (not_39_out, i4);
  not not_40 (not_40_out, i3);
  and and_18 (and_18_out, not_40_out, not_41_out);
  not not_41 (not_41_out, i4);
  and and_19 (and_19_out, i2, i4);
  and and_20 (and_20_out, i1, i3);
  not not_42 (not_42_out, i1);
  not not_43 (not_43_out, i2);
  not not_44 (not_44_out, i4);
  not not_45 (not_45_out, i4);
  or or_1 (b2, and_1_out, and_2_out, and_3_out);
  and and_21 (and_21_out, i1, i2, not_7_out, not_8_out);
  or or_2 (b3, and_21_out, and_22_out);
  and and_22 (and_22_out, i1, i2, i3, i4);
  or or_3 (b4, and_4_out, and_5_out, and_6_out, and_7_out);
  or or_4 (b5, and_8_out, and_9_out, and_10_out);
  and and_23 (and_23_out, not_17_out, not_18_out, not_19_out, i4);
  and and_24 (and_24_out, not_20_out, not_21_out, i3, not_22_out);
  and and_25 (and_25_out, i1, not_23_out, not_24_out, not_25_out);
  and and_26 (and_26_out, i1, not_26_out, i3, i4);
  and and_27 (and_27_out, not_27_out, not_28_out, i3, i4);
  or or_5 (b7, and_27_out, and_28_out);
  and and_28 (and_28_out, i1, i2, not_29_out);
  or or_6 (b8, and_11_out, and_12_out, and_13_out, and_14_out, and_15_out);
  or or_7 (b9, and_16_out, and_17_out, and_18_out, and_19_out, and_20_out);
  and and_29 (and_29_out, not_42_out, not_43_out, i3, not_44_out);
  or or_8 (b10, and_29_out, and_30_out);
  and and_30 (and_30_out, i1, i2, i3, not_45_out);
  or or_9 (b6, and_23_out, and_24_out, and_25_out, and_26_out);
  LED led_1 (.in(1'b1));
  LED led_2 (.in(b2));
  LED led_3 (.in(b3));
  LED led_4 (.in(b7));
  LED led_5 (.in(b5));
  LED led_6 (.in(b4));
  LED led_7 (.in(b6));
  LED led_8 (.in(b10));
  LED led_9 (.in(b9));
  LED led_10 (.in(b8));
  LED led_11 (.in(1'b0));

  assign b1 = 1'b1;
  assign b11 = 1'b0;
endmodule

module code_128_NAND (
  input  i1,
  input  i2,
  input  i3,
  input  i4,
  output b1,
  output b2,
  output b3,
  output b4,
  output b5,
  output b6,
  output b7,
  output b8,
  output b9,
  output b10,
  output b11
);

  wire I1_out, I2_2_out, I2_3_out, I2_out, I3_out, I4_out, nand_1_out, nand_2_out, nand_3_out, nand_4_out,
       nand_5_out, nand_6_out, nand_7_out, nand_8_out, nand_9_out, nand_10_out, nand_11_out, nand_12_out,
       nand_13_out, nand_14_out, nand_15_out, nand_16_out, nand_17_out, nand_18_out, nand_19_out,
       nand_20_out, nand_21_out, nand_22_out, nand_23_out, nand_24_out, nand_25_out, nand_26_out,
       nand_27_out, nand_28_out, nand_29_out, nand_30_out, nand_31_out, nand_32_out, nand_33_out,
       nand_34_out, nand_35_out, nand_36_out, nand_37_out, nand_38_out, nand_39_out, nand_40_out,
       nand_41_out, nand_42_out, nand_43_out, nand_44_out, nand_45_out, nand_46_out, nand_47_out,
       nand_48_out, nand_49_out, nand_50_out, nand_51_out, nand_52_out, nand_53_out, nand_54_out,
       nand_55_out, nand_56_out, nand_57_out, nand_58_out, nand_59_out, nand_60_out, nand_61_out,
       nand_62_out, nand_63_out, nand_64_out, nand_65_out, nand_66_out, W1_out, W2_out, W3_out;

  nand u_I1 (I1_out, i1, i1);
  nand u_I2 (I2_out, i2, i2);
  nand u_I3 (I3_out, i3, i3);
  nand I2_2 (I2_2_out, i2, i2);
  nand u_I4 (I4_out, i4, i4);
  nand I2_3 (I2_3_out, i2, i2);
  nand nand_1 (nand_1_out, i3, i3);
  nand nand_2 (nand_2_out, i4, i4);
  nand nand_3 (nand_3_out, i1, i1);
  nand nand_4 (nand_4_out, i3, i3);
  nand nand_5 (nand_5_out, i4, i4);
  nand nand_6 (nand_6_out, i1, i1);
  nand nand_7 (nand_7_out, i4, i4);
  nand nand_8 (nand_8_out, i2, i2);
  nand nand_9 (nand_9_out, i3, i3);
  nand nand_10 (nand_10_out, i4, i4);
  nand nand_11 (nand_11_out, i1, i1);
  nand nand_12 (nand_12_out, i2, i2);
  nand nand_13 (nand_13_out, i3, i3);
  nand nand_14 (nand_14_out, i1, i1);
  nand nand_15 (nand_15_out, i2, i2);
  nand nand_16 (nand_16_out, i4, i4);
  nand nand_17 (nand_17_out, i2, i2);
  nand nand_18 (nand_18_out, i3, i3);
  nand nand_19 (nand_19_out, i4, i4);
  nand nand_20 (nand_20_out, i2, i2);
  nand nand_21 (nand_21_out, i1, i1);
  nand nand_22 (nand_22_out, i2, i2);
  nand nand_23 (nand_23_out, i3, i3);
  nand nand_24 (nand_24_out, i1, i1);
  nand nand_25 (nand_25_out, i3, i3);
  nand nand_26 (nand_26_out, i1, i1);
  nand nand_27 (nand_27_out, i2, i2);
  nand nand_28 (nand_28_out, i3, i3);
  nand nand_29 (nand_29_out, i4, i4);
  nand nand_30 (nand_30_out, i1, i1);
  nand nand_31 (nand_31_out, i3, i3);
  nand nand_32 (nand_32_out, i2, i2);
  nand nand_33 (nand_33_out, i4, i4);
  nand nand_34 (nand_34_out, i3, i3);
  nand nand_35 (nand_35_out, i4, i4);
  nand nand_36 (nand_36_out, i1, i1);
  nand nand_37 (nand_37_out, i2, i2);
  nand nand_38 (nand_38_out, i4, i4);
  nand nand_39 (nand_39_out, i4, i4);
  nand W1 (W1_out, I1_out, I2_out, I3_out);
  nand W2 (W2_out, I2_2_out, i3, I4_out);
  nand W3 (W3_out, i1, I2_3_out, i4);
  nand nand_40 (nand_40_out, i1, i2, nand_1_out, nand_2_out);
  nand nand_41 (nand_41_out, i1, i2, i3, i4);
  nand nand_42 (nand_42_out, nand_3_out, nand_4_out, nand_5_out);
  nand nand_43 (nand_43_out, nand_6_out, i3, i4);
  nand nand_44 (nand_44_out, i2, nand_7_out);
  nand nand_45 (nand_45_out, i1, i2);
  nand nand_46 (nand_46_out, nand_8_out, nand_9_out);
  nand nand_47 (nand_47_out, i3, nand_10_out);
  nand nand_48 (nand_48_out, i2, i4);
  nand nand_49 (nand_49_out, nand_11_out, nand_12_out, nand_13_out, i4);
  nand nand_50 (nand_50_out, nand_14_out, nand_15_out, i3, nand_16_out);
  nand nand_51 (nand_51_out, i1, nand_17_out, nand_18_out, nand_19_out);
  nand nand_52 (nand_52_out, i1, nand_20_out, i3, i4);
  nand nand_53 (nand_53_out, nand_21_out, nand_22_out, i3, i4);
  nand nand_54 (nand_54_out, i1, i2, nand_23_out);
  nand nand_55 (nand_55_out, nand_24_out, nand_25_out);
  nand nand_56 (nand_56_out, nand_26_out, nand_27_out, i4);
  nand nand_57 (nand_57_out, nand_28_out, i4);
  nand nand_58 (nand_58_out, i2, nand_29_out);
  nand nand_59 (nand_59_out, i1, i2);
  nand nand_60 (nand_60_out, nand_30_out, nand_31_out);
  nand nand_61 (nand_61_out, nand_32_out, nand_33_out);
  nand nand_62 (nand_62_out, nand_34_out, nand_35_out);
  nand nand_63 (nand_63_out, i2, i4);
  nand nand_64 (nand_64_out, i1, i3);
  nand nand_65 (nand_65_out, nand_36_out, nand_37_out, i3, nand_38_out);
  nand nand_66 (nand_66_out, i1, i2, i3, nand_39_out);
  nand O (b2, W1_out, W2_out, W3_out);
  nand nand_67 (b3, nand_40_out, nand_41_out);
  nand nand_68 (b4, nand_42_out, nand_43_out, nand_44_out, nand_45_out);
  nand nand_69 (b5, nand_46_out, nand_47_out, nand_48_out);
  nand nand_70 (b6, nand_49_out, nand_50_out, nand_51_out, nand_52_out);
  nand nand_71 (b7, nand_53_out, nand_54_out);
  nand nand_72 (b8, nand_55_out, nand_56_out, nand_57_out, nand_58_out, nand_59_out);
  nand nand_73 (b9, nand_60_out, nand_61_out, nand_62_out, nand_63_out, nand_64_out);
  nand nand_74 (b10, nand_65_out, nand_66_out);
  LED led_1 (.in(1'b1));
  LED led_2 (.in(b4));
  LED led_3 (.in(b3));
  LED led_4 (.in(b5));
  LED led_5 (.in(b2));
  LED led_6 (.in(b6));
  LED led_7 (.in(b8));
  LED led_8 (.in(b9));
  LED led_9 (.in(b7));
  LED led_10 (.in(b10));
  LED led_11 (.in(1'b0));

  assign b1 = 1'b1;
  assign b11 = 1'b0;

  // Notes on the sheet:
  //   I3
  //   I1
  //   I4
  //   not 0(zero)
  //   O as in letter o. 
endmodule
